# Fritzing sketch gasMonitor (saved by Fritzing 0.9.1b)
perfboards: 1

parts:
  Arduino = Arduino Pro Mini v13
  R1 = Resistor [tolerance=±5% resistance=1k package=THT]
  R2 = Resistor [tolerance=±5% resistance=1k package=THT]
  LED1 = LED - 5mm [color="Red (633nm)" package="5 mm [THT]"]
  LED2 = LED - 5mm [color="Green (570nm)" package="5 mm [THT]"]
  DHT1 = DHT22 Humidity and Temperature Sensor
  S1 = Reed switch [package=THT]
  R3 = Resistor [tolerance=±5% resistance=10k package=THT]
  RF_433MHz = RF-LINK_TX [package=rf-link_tx]
  Power_5v = Power plug
  J1 = female pin header, 1 pin [form="♀ (female)"]

nets:
  VCC: Arduino.VCC, DHT1.VDD, S1.pin_2, RF_433MHz.+5V, Power_5v.VCC
  GND: Arduino.GND, LED1.cathode, LED2.cathode, DHT1.GND, R3.Pin_1, RF_433MHz.GND, Power_5v.GND
  N1: Arduino.D13/SCK, R2.Pin_1
  N2: Arduino.D12/MISO, R1.Pin_1
  N3: Arduino.D7, RF_433MHz.DATA
  N4: Arduino.D5_PWM, DHT1.DATA
  N5: Arduino.D2, S1.pin_1, R3.Pin_0
  N6: R1.Pin_0, LED2.anode
  N7: R2.Pin_0, LED1.anode
  N8: RF_433MHz.ANT, J1.pin1
